# Fritzing sketch 선풍기 (saved by Fritzing 0.9.3b)
breadboards: 1

parts:
  D1 = Rectifier Diode [part_number=1N4001 package="300 mil [THT]"]
  Q1 = NPN-Transistor [package="TO92 [THT]"]
  부품1 = Arduino Uno (Rev3)
  R1 = Resistor [tolerance=±10% resistance=1k package=THT]
  M1 = DC Motor
  R2 = Resistor [tolerance=±5% resistance=220 package=THT]  # not connected
  S1 = Pushbutton [package="[THT]"]
  S2 = Pushbutton [package="[THT]"]
  7_Segment1 = 7 Segment Display
  J1 = Basic Servo

nets:
  5V: D1.cathode, 부품1.5V, M1.pin_2, J1.vcc
  N1: Q1.E, S1.Pin_3, S1.Pin_4, S2.Pin_3, S2.Pin_4
  N2: Q1.C, M1.pin_1
  N3: 부품1.D9_PWM, J1.pulse
  N4: 부품1.D10_PWM/SS, 7_Segment1.Segment_D
  N5: 부품1.D11_PWM/MOSI, 7_Segment1.Segment_G, 7_Segment1.Segment_F
  N6: 부품1.D2, S2.Pin_1, S2.Pin_2
  N7: 부품1.D3_PWM, S1.Pin_1, S1.Pin_2
  N8: 부품1.D5_PWM, R1.Pin_0
  N9: 부품1.D6_PWM, 7_Segment1.Segment_B, 7_Segment1.Segment_A
  GND: 부품1.GND, J1.gnd
