# Fritzing sketch ar07_4digit (saved by Fritzing 0.9.3b)
breadboards: 1

parts:
  R1 = Resistor [tolerance=±5% resistance=330 package=THT]
  R2 = Resistor [tolerance=±5% resistance=330 package=THT]
  R3 = Resistor [tolerance=±5% resistance=330 package=THT]
  R4 = Resistor [tolerance=±5% resistance=330 package=THT]
  R5 = Resistor [tolerance=±5% resistance=330 package=THT]
  R6 = Resistor [tolerance=±5% resistance=330 package=THT]
  R7 = Resistor [tolerance=±5% resistance=330 package=THT]
  R8 = Resistor [tolerance=±5% resistance=330 package=THT]
  부품1 = Arduino Uno (Rev3)
  U1 = 7-SEGMENT-4DIGIT [package=7-segment-4digit-5641]
  R9 = Resistor [tolerance=±5% resistance=220 package=THT]
  R10 = Resistor [tolerance=±5% resistance=220 package=THT]
  R11 = Resistor [tolerance=±5% resistance=220 package=THT]
  R12 = Resistor [tolerance=±5% resistance=220 package=THT]
  R13 = Resistor [tolerance=±5% resistance=220 package=THT]
  R14 = Resistor [tolerance=±5% resistance=220 package=THT]
  R15 = Resistor [tolerance=±5% resistance=220 package=THT]
  R16 = Resistor [tolerance=±5% resistance=220 package=THT]

nets:
  N1: R1.Pin_0, R3.Pin_0, R5.Pin_0, R6.Pin_0, R8.Pin_0
  N2: R1.Pin_1, R3.Pin_1, R5.Pin_1, R6.Pin_1, R8.Pin_1
  N3: R2.Pin_0, R4.Pin_0, R7.Pin_0
  N4: R2.Pin_1, R4.Pin_1, R7.Pin_1
  N5: 부품1.D8, R16.Pin_0
  N6: 부품1.D9_PWM, R11.Pin_0
  N7: 부품1.D10_PWM/SS, U1.DIG1
  N8: 부품1.D11_PWM/MOSI, U1.DIG2
  N9: 부품1.D12/MISO, U1.DIG3
  N10: 부품1.D13/SCK, U1.DIG4
  N11: 부품1.D2, R13.Pin_1
  N12: 부품1.D3_PWM, R14.Pin_0
  N13: 부품1.D4, R15.Pin_0
  N14: 부품1.D5_PWM, R10.Pin_0
  N15: 부품1.D6_PWM, R9.Pin_1
  N16: 부품1.D7, R12.Pin_1
  N17: U1.A, R13.Pin_0
  N18: U1.B, R14.Pin_1
  N19: U1.C, R15.Pin_1
  N20: U1.D, R10.Pin_1
  N21: U1.E, R9.Pin_0
  N22: U1.F, R12.Pin_0
  N23: U1.G, R16.Pin_1
  N24: U1.DP, R11.Pin_1

custom parts:
  7-SEGMENT-4DIGIT: if you need make parts, send me e-mail and write. Price 1 part=0.9 WMZ (http://www.wmtransfer.com/) ~ 0.9 Euro
